// Logisim project memoria.circ as structural Verilog: 2 circuits, main circuit Mem Instr
module Mem_Instr (
  input  [31:0] PC_Adress,
  output [31:0] out_2
);

  ROM #(.addrWidth(24), .dataWidth(32)) rom_1 (.addr(PC_Adress[25:2]), .data(out_2));  // open: sel

  // Notes on the sheet:
  //   contents of rom_1 (hex, n*v repeats v):
  //   2
endmodule

// MemWrite
module Mem_Dados (
  input  MemWrite,
  input  MemRead,
  output [31:0] A,
  output [31:0] out_4,
  output [31:0] B
);

  wire clock_1_out;

  Clock clock_1 (.out(clock_1_out));
  RAM #(.addrWidth(24), .dataWidth(32), .bus("separate")) ram_1 (
    .addr(A[23:0]), .din(B), .data(out_4), .str(MemWrite), .clk(clock_1_out), .ld(MemRead));  // open: sel, clr
  // Pins of 24 and 32 bits meet at A
endmodule
