// Logisim project registrador.circ as structural Verilog: 1 circuit, main circuit banco de registradores
module banco_de_registradores (
  input  [4:0] LR1,
  input  [4:0] LR2,
  input  [31:0] WD,
  input  [4:0] WR,
  input  RegWrite,
  output [31:0] LD1,
  output [31:0] LD2
);

  wire Clock, demultiplexer_2_out1, demultiplexer_2_out2, demultiplexer_2_out3, demultiplexer_2_out4,
       demultiplexer_2_out5, demultiplexer_2_out6, demultiplexer_2_out7, demultiplexer_2_out8,
       demultiplexer_2_out9, demultiplexer_2_out10, demultiplexer_2_out11, demultiplexer_2_out12,
       demultiplexer_2_out13, demultiplexer_2_out14, demultiplexer_2_out15, demultiplexer_2_out16,
       demultiplexer_2_out17, demultiplexer_2_out18, demultiplexer_2_out19, demultiplexer_2_out20,
       demultiplexer_2_out21, demultiplexer_2_out22, demultiplexer_2_out23, demultiplexer_2_out24,
       demultiplexer_2_out25, demultiplexer_2_out26, demultiplexer_2_out27, demultiplexer_2_out28,
       demultiplexer_2_out29, demultiplexer_2_out30, demultiplexer_2_out31, undriven;
  wire [31:0] a0_q, a1_q, a2_q, a3_q, at_q, demultiplexer_1_out0, demultiplexer_1_out1, demultiplexer_1_out2,
       demultiplexer_1_out3, demultiplexer_1_out4, demultiplexer_1_out5, demultiplexer_1_out6,
       demultiplexer_1_out7, demultiplexer_1_out8, demultiplexer_1_out9, demultiplexer_1_out10,
       demultiplexer_1_out11, demultiplexer_1_out12, demultiplexer_1_out13, demultiplexer_1_out14,
       demultiplexer_1_out15, demultiplexer_1_out16, demultiplexer_1_out17, demultiplexer_1_out18,
       demultiplexer_1_out19, demultiplexer_1_out20, demultiplexer_1_out21, demultiplexer_1_out22,
       demultiplexer_1_out23, demultiplexer_1_out24, demultiplexer_1_out25, demultiplexer_1_out26,
       demultiplexer_1_out27, demultiplexer_1_out28, demultiplexer_1_out29, demultiplexer_1_out30,
       demultiplexer_1_out31, fp_q, gp_q, k0_q, k1_q, ra_q, s0_q, s1_q, s2_q, s3_q, s4_q, s5_q, s6_q, s7_q,
       sp_q, t0_q, t1_q, t2_q, t3_q, t4_q, t5_q, t6_q, t7_q, t8_q, t9_q, v0_q, v1_q, zero_q;

  Demultiplexer #(.select(5), .width(32), .enable("false")) demultiplexer_1 (
    .out0(demultiplexer_1_out0), .out1(demultiplexer_1_out1), .out2(demultiplexer_1_out2),
    .out3(demultiplexer_1_out3), .out4(demultiplexer_1_out4), .out5(demultiplexer_1_out5),
    .out6(demultiplexer_1_out6), .out7(demultiplexer_1_out7), .out8(demultiplexer_1_out8),
    .out9(demultiplexer_1_out9), .out10(demultiplexer_1_out10), .out11(demultiplexer_1_out11),
    .out12(demultiplexer_1_out12), .out13(demultiplexer_1_out13), .out14(demultiplexer_1_out14),
    .out15(demultiplexer_1_out15), .out16(demultiplexer_1_out16), .out17(demultiplexer_1_out17),
    .out18(demultiplexer_1_out18), .out19(demultiplexer_1_out19), .out20(demultiplexer_1_out20),
    .out21(demultiplexer_1_out21), .out22(demultiplexer_1_out22), .out23(demultiplexer_1_out23),
    .out24(demultiplexer_1_out24), .out25(demultiplexer_1_out25), .out26(demultiplexer_1_out26),
    .out27(demultiplexer_1_out27), .out28(demultiplexer_1_out28), .out29(demultiplexer_1_out29),
    .out30(demultiplexer_1_out30), .out31(demultiplexer_1_out31), .in(WD), .sel(WR));
  Clock clock_1 (.out(Clock));
  Demultiplexer #(.select(5), .enable("false")) demultiplexer_2 (
    .out1(demultiplexer_2_out1), .out2(demultiplexer_2_out2), .out3(demultiplexer_2_out3),
    .out4(demultiplexer_2_out4), .out5(demultiplexer_2_out5), .out6(demultiplexer_2_out6),
    .out7(demultiplexer_2_out7), .out8(demultiplexer_2_out8), .out9(demultiplexer_2_out9),
    .out10(demultiplexer_2_out10), .out11(demultiplexer_2_out11), .out12(demultiplexer_2_out12),
    .out13(demultiplexer_2_out13), .out14(demultiplexer_2_out14), .out15(demultiplexer_2_out15),
    .out16(demultiplexer_2_out16), .out17(demultiplexer_2_out17), .out18(demultiplexer_2_out18),
    .out19(demultiplexer_2_out19), .out20(demultiplexer_2_out20), .out21(demultiplexer_2_out21),
    .out22(demultiplexer_2_out22), .out23(demultiplexer_2_out23), .out24(demultiplexer_2_out24),
    .out25(demultiplexer_2_out25), .out26(demultiplexer_2_out26), .out27(demultiplexer_2_out27),
    .out28(demultiplexer_2_out28), .out29(demultiplexer_2_out29), .out30(demultiplexer_2_out30),
    .out31(demultiplexer_2_out31), .in(RegWrite), .sel(WR));  // open: out0
  Register #(.width(32)) zero (.D(demultiplexer_1_out0), .Q(zero_q));  // open: en, clk, clr
  Register #(.width(32)) at (.D(demultiplexer_1_out1), .en(demultiplexer_2_out1), .Q(at_q), .clk(Clock));  // open: clr
  Register #(.width(32)) v0 (.D(demultiplexer_1_out2), .en(demultiplexer_2_out2), .Q(v0_q), .clk(Clock));  // open: clr
  Register #(.width(32)) v1 (.D(demultiplexer_1_out3), .en(demultiplexer_2_out3), .Q(v1_q), .clk(Clock));  // open: clr
  Register #(.width(32)) a0 (.D(demultiplexer_1_out4), .en(demultiplexer_2_out4), .Q(a0_q), .clk(Clock));  // open: clr
  Register #(.width(32)) a1 (.D(demultiplexer_1_out5), .en(demultiplexer_2_out5), .Q(a1_q), .clk(Clock));  // open: clr
  Register #(.width(32)) a2 (.D(demultiplexer_1_out6), .en(demultiplexer_2_out6), .Q(a2_q), .clk(Clock));  // open: clr
  Register #(.width(32)) a3 (
    .D(demultiplexer_1_out7), .en(demultiplexer_2_out7), .Q(a3_q), .clk(Clock), .clr(undriven));
  Register #(.width(32)) s0 (
    .D(demultiplexer_1_out16), .en(demultiplexer_2_out16), .Q(s0_q), .clk(Clock));  // open: clr
  Register #(.width(32)) s1 (
    .D(demultiplexer_1_out17), .en(demultiplexer_2_out17), .Q(s1_q), .clk(Clock));  // open: clr
  Register #(.width(32)) s2 (
    .D(demultiplexer_1_out18), .en(demultiplexer_2_out18), .Q(s2_q), .clk(Clock));  // open: clr
  Register #(.width(32)) s3 (
    .D(demultiplexer_1_out19), .en(demultiplexer_2_out19), .Q(s3_q), .clk(Clock));  // open: clr
  Register #(.width(32)) s4 (
    .D(demultiplexer_1_out20), .en(demultiplexer_2_out20), .Q(s4_q), .clk(Clock));  // open: clr
  Register #(.width(32)) s5 (
    .D(demultiplexer_1_out21), .en(demultiplexer_2_out21), .Q(s5_q), .clk(Clock));  // open: clr
  Register #(.width(32)) s6 (
    .D(demultiplexer_1_out22), .en(demultiplexer_2_out22), .Q(s6_q), .clk(Clock));  // open: clr
  Register #(.width(32)) s7 (
    .D(demultiplexer_1_out23), .en(demultiplexer_2_out23), .Q(s7_q), .clk(Clock));  // open: clr
  Register #(.width(32)) t0 (.D(demultiplexer_1_out8), .en(demultiplexer_2_out8), .Q(t0_q), .clk(Clock));  // open: clr
  Register #(.width(32)) t1 (.D(demultiplexer_1_out9), .en(demultiplexer_2_out9), .Q(t1_q), .clk(Clock));  // open: clr
  Register #(.width(32)) t2 (
    .D(demultiplexer_1_out10), .en(demultiplexer_2_out10), .Q(t2_q), .clk(Clock));  // open: clr
  Register #(.width(32)) t3 (
    .D(demultiplexer_1_out11), .en(demultiplexer_2_out11), .Q(t3_q), .clk(Clock));  // open: clr
  Register #(.width(32)) t4 (
    .D(demultiplexer_1_out12), .en(demultiplexer_2_out12), .Q(t4_q), .clk(Clock));  // open: clr
  Register #(.width(32)) t5 (
    .D(demultiplexer_1_out13), .en(demultiplexer_2_out13), .Q(t5_q), .clk(Clock));  // open: clr
  Register #(.width(32)) t6 (
    .D(demultiplexer_1_out14), .en(demultiplexer_2_out14), .Q(t6_q), .clk(Clock));  // open: clr
  Register #(.width(32)) t7 (
    .D(demultiplexer_1_out15), .en(demultiplexer_2_out15), .Q(t7_q), .clk(Clock));  // open: clr
  Register #(.width(32)) t8 (
    .D(demultiplexer_1_out24), .en(demultiplexer_2_out24), .Q(t8_q), .clk(Clock));  // open: clr
  Register #(.width(32)) t9 (
    .D(demultiplexer_1_out25), .en(demultiplexer_2_out25), .Q(t9_q), .clk(Clock));  // open: clr
  Register #(.width(32)) k0 (
    .D(demultiplexer_1_out26), .en(demultiplexer_2_out26), .Q(k0_q), .clk(Clock));  // open: clr
  Register #(.width(32)) k1 (
    .D(demultiplexer_1_out27), .en(demultiplexer_2_out27), .Q(k1_q), .clk(Clock));  // open: clr
  Register #(.width(32)) gp (
    .D(demultiplexer_1_out28), .en(demultiplexer_2_out28), .Q(gp_q), .clk(Clock));  // open: clr
  Register #(.width(32)) sp (
    .D(demultiplexer_1_out29), .en(demultiplexer_2_out29), .Q(sp_q), .clk(Clock));  // open: clr
  Register #(.width(32)) fp (
    .D(demultiplexer_1_out30), .en(demultiplexer_2_out30), .Q(fp_q), .clk(Clock));  // open: clr
  Register #(.width(32)) ra (
    .D(demultiplexer_1_out31), .en(demultiplexer_2_out31), .Q(ra_q), .clk(Clock));  // open: clr
  Multiplexer #(.select(5), .width(32), .enable("false")) multiplexer_1 (
    .in0(zero_q), .in1(at_q), .in2(v0_q), .in3(v1_q), .in4(a0_q), .in5(a1_q), .in6(a2_q), .in7(a3_q),
    .in8(t0_q), .in9(t1_q), .in10(t2_q), .in11(t3_q), .in12(t4_q), .in13(t5_q), .in14(t6_q), .in15(t7_q),
    .in16(s0_q), .in17(s1_q), .in18(s2_q), .in19(s3_q), .in20(s4_q), .in21(s5_q), .in22(s6_q), .in23(s7_q),
    .in24(t8_q), .in25(t9_q), .in26(k0_q), .in27(k1_q), .in28(gp_q), .in29(sp_q), .in30(fp_q), .in31(ra_q),
    .out(LD1), .sel(LR1));
  Multiplexer #(.select(5), .width(32), .enable("false")) multiplexer_2 (
    .in0(zero_q), .in1(at_q), .in2(v0_q), .in3(v1_q), .in4(a0_q), .in5(a1_q), .in6(a2_q), .in7(a3_q),
    .in8(t0_q), .in9(t1_q), .in10(t2_q), .in11(t3_q), .in12(t4_q), .in13(t5_q), .in14(t6_q), .in15(t7_q),
    .in16(s0_q), .in17(s1_q), .in18(s2_q), .in19(s3_q), .in20(s4_q), .in21(s5_q), .in22(s6_q), .in23(s7_q),
    .in24(t8_q), .in25(t9_q), .in26(k0_q), .in27(k1_q), .in28(gp_q), .in29(sp_q), .in30(fp_q), .in31(ra_q),
    .out(LD2), .sel(LR2));
endmodule
